# Fritzing sketch temperature_sensor (saved by Fritzing 0.9.3b)
circuit board: 5.4cm x 3.3cm
breadboards: 1

parts:
  Part1 = Adafruit Feather HUZZAH ESP8266 [part_number="Adafruit #2821"]
  T1 = LM35 Temperature Sensor [package="TO92 [THT]"]

nets:
  N1: Part1.ADC, T1.Vout
  GND: Part1.GND, T1.GND
  N2: Part1.3.3V, T1.+Vs

custom parts:
  Adafruit Feather HUZZAH ESP8266: his is the Adafruit Feather HUZZAH ESP8266 - our take on an 'all-in-one' ESP8266 WiFi development board with built in USB and battery charging. Its an ESP8266 WiFi module with all the extras you need, ready to rock! We have other boards in the Feather family, check'em out here. At the Feather HUZZAH's heart is an ESP8266 WiFi microcontroller clocked at 80 MHz and at 3.3V logic. This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
